# Fritzing sketch wiring (saved by Fritzing 0.9.2b)

parts:
  Composant1 = Arduino Leonardo (Rev3b)
  J1 = Infrared Proximity Sensor
  J2 = Infrared Proximity Sensor

nets:
  VCC: Composant1.5V, J1.Vcc, J2.Vcc
  GND: Composant1.GND, J1.GND, J2.GND
  N1: Composant1.A0, J1.Vout
